// Logisim project portas_logicas_1.circ as structural Verilog: 1 circuit, main circuit Porta XOR
module Porta_XOR (
  input  A,
  input  A_2,
  input  A_3,
  input  B,
  input  B_2,
  input  A_4,
  input  A_5,
  input  A_6,
  input  B_3,
  input  B_4,
  input  B_5,
  output out_12,
  output out_13,
  output out_14,
  output out_15,
  output out_16,
  output out_17
);

  and and_1 (out_12, A, B);
  nand nand_1 (out_15, A_4, B_3);
  or or_1 (out_13, A_2, B_2);
  nor nor_1 (out_16, A_5, B_4);
  not not_1 (out_14, A_3);
  xor xor_1 (out_17, A_6, B_5);

  // Notes on the sheet:
  //   Porta AND
  //   Porta NAND
  //   Porta OR
  //   Porta NOR
  //   Porta NOT
  //   Porta XOR
endmodule
