// Logisim project portas_logicas_2.circ as structural Verilog: 1 circuit, main circuit Porta XOR
module Porta_XOR (
  input  A,
  input  B,
  output Porta_AND,
  output Porta_OR,
  output Porta_NOT,
  output out_6,
  output Porta_NOR,
  output out_8
);

  not not_1 (Porta_NOT, A);
  and and_1 (Porta_AND, A, B);
  or or_1 (Porta_OR, A, B);
  nand nand_1 (out_6, A, B);
  nor nor_1 (Porta_NOR, A, B);
  xor xor_1 (out_8, A, B);

  // Notes on the sheet:
  //   Porta NAND
  //   Porta XOR
endmodule
