// Logisim project portas_logicas_3.circ as structural Verilog: 1 circuit, main circuit Porta XOR
module Porta_XOR (
  input  A,
  input  B,
  input  C,
  output S,
  output S_2,
  output S_3,
  output out_7,
  output Porta_NOR,
  output out_9
);

  not not_1 (S_3, A);
  and and_1 (S, A, B, C);
  or or_1 (S_2, A, B, C);
  nand nand_1 (out_7, A, B, C);
  nor nor_1 (Porta_NOR, A, B, C);
  ExactlyOne xor_1 (.out(out_9), .in0(A), .in1(B), .in2(C));

  // Notes on the sheet:
  //   Porta AND
  //   Porta OR
  //   Porta NOT
  //   Porta NAND
  //   Porta XOR
endmodule
