// Logisim project comparador_2bits_completo_mintermos.circ as structural Verilog: 1 circuit, main circuit main
module main (
  input  A,
  input  B,
  input  C,
  input  D,
  output F1__AB___CD,
  output F2__AB___CD,
  output F3__AB___CD
);

  wire _0_out, _1_out, _2_out, _3_out, _4_out, _5_out, _6_out, _7_out, _8_out, _9_out, _10_out, _11_out,
       _12_out, _13_out, _14_out, _15_out, not_1_out, not_2_out, not_3_out, not_4_out, not_5_out, not_6_out,
       not_7_out, not_8_out, not_9_out, not_10_out, not_11_out, not_12_out, not_13_out, not_14_out,
       not_15_out, not_16_out, not_17_out, not_18_out, not_19_out, not_20_out, not_21_out, not_22_out,
       not_23_out, not_24_out, not_25_out, not_26_out, not_27_out, not_28_out, not_29_out, not_30_out,
       not_31_out, not_32_out;

  not not_1 (not_1_out, A);
  not not_2 (not_2_out, B);
  and _0 (_0_out, not_1_out, not_2_out, not_7_out, not_6_out);
  not not_3 (not_3_out, C);
  not not_4 (not_4_out, B);
  not not_5 (not_5_out, A);
  not not_6 (not_6_out, D);
  not not_7 (not_7_out, C);
  and _1 (_1_out, not_5_out, not_4_out, not_3_out, D);
  not not_8 (not_8_out, B);
  not not_9 (not_9_out, A);
  not not_10 (not_10_out, A);
  not not_11 (not_11_out, D);
  and _2 (_2_out, not_9_out, not_8_out, C, not_11_out);
  not not_12 (not_12_out, A);
  not not_13 (not_13_out, B);
  and _3 (_3_out, not_10_out, not_13_out, C, D);
  or F1 (F1__AB___CD, _0_out, _5_out, _10_out, _15_out);
  not not_14 (not_14_out, D);
  not not_15 (not_15_out, C);
  not not_16 (not_16_out, C);
  not not_17 (not_17_out, A);
  and _5 (_5_out, not_17_out, B, not_15_out, D);
  and _4 (_4_out, not_12_out, B, not_16_out, not_14_out);
  not not_18 (not_18_out, D);
  not not_19 (not_19_out, A);
  and _6 (_6_out, not_19_out, B, C, not_18_out);
  not not_20 (not_20_out, A);
  and _7 (_7_out, not_20_out, B, C, D);
  or F2 (F2__AB___CD, _1_out, _2_out, _3_out, _6_out, _7_out, _11_out);
  not not_21 (not_21_out, D);
  not not_22 (not_22_out, B);
  not not_23 (not_23_out, B);
  not not_24 (not_24_out, C);
  and _9 (_9_out, A, not_22_out, not_27_out, D);
  and _8 (_8_out, A, not_23_out, not_24_out, not_21_out);
  not not_25 (not_25_out, B);
  not not_26 (not_26_out, D);
  not not_27 (not_27_out, C);
  and _10 (_10_out, A, not_25_out, C, not_26_out);
  not not_28 (not_28_out, B);
  and _11 (_11_out, A, not_28_out, C, D);
  or F3 (F3__AB___CD, _4_out, _8_out, _9_out, _12_out, _13_out, _14_out);
  not not_29 (not_29_out, D);
  not not_30 (not_30_out, C);
  and _12 (_12_out, A, B, not_30_out, not_29_out);
  not not_31 (not_31_out, C);
  and _13 (_13_out, A, B, not_31_out, D);
  and _14 (_14_out, A, B, C, not_32_out);
  not not_32 (not_32_out, D);
  and _15 (_15_out, A, B, C, D);

  // Notes on the sheet:
  //   F1(A,B,C,D) = ∑ABCD(0,5,10,15) 
  //   F1(A,B,C,D) = ∑ABCD(1,2,3,6,7,11)
  //   F3(A,B,C,D) = ∑ABCD(4,8,9,12,13,14)
  //   Comparador de 2 bits - Mintermos:
endmodule
