// Logisim project incrementador_bcd_karnaugh.circ as structural Verilog: 1 circuit, main circuit main
module main (
  input  A,
  input  B,
  input  C,
  input  D,
  output W,
  output X,
  output Y,
  output Z
);

  wire and_1_out, and_2_out, and_3_out, and_4_out, and_5_out, and_6_out, and_7_out, not_1_out, not_2_out,
       not_3_out, not_4_out, not_5_out, not_6_out, not_7_out, not_8_out, not_9_out;

  not not_1 (not_1_out, D);
  not not_2 (not_2_out, A);
  not not_3 (not_3_out, D);
  not not_4 (not_4_out, C);
  not not_5 (not_5_out, B);
  not not_6 (not_6_out, A);
  not not_7 (not_7_out, C);
  not not_8 (not_8_out, A);
  not not_9 (not_9_out, D);
  not not_10 (Z, D);
  and and_1 (and_1_out, A, not_1_out);
  and and_2 (and_2_out, not_2_out, B, C, D);
  and and_3 (and_3_out, B, not_3_out);
  and and_4 (and_4_out, B, not_4_out);
  and and_5 (and_5_out, not_5_out, C, D);
  and and_6 (and_6_out, not_6_out, not_7_out, D);
  and and_7 (and_7_out, not_8_out, C, not_9_out);
  or or_1 (W, and_1_out, and_2_out);
  or or_2 (X, and_3_out, and_4_out, and_5_out);
  or or_3 (Y, and_6_out, and_7_out);

  // Notes on the sheet:
  //   Incrementador BCD:
  //   (Mapa de Karnaugh)
  //   W = AD'+A'BCD
  //   X = BD'+ BC' + B'CD 
  //   Y = A'C'D + A'CD'
  //   Z =D'
endmodule
