// Logisim project adicao_binaria_vai_um.circ as structural Verilog: 1 circuit, main circuit main
module main (
  input  A,
  input  B,
  input  C,
  output C_out,
  output S
);

  wire and_1_out, and_2_out, and_3_out, and_4_out, and_5_out, and_6_out, and_7_out, not_1_out, not_2_out,
       not_3_out, not_4_out, not_5_out, not_6_out;

  or or_1 (C_out, and_1_out, and_2_out, and_3_out);
  and and_1 (and_1_out, A, B);
  and and_2 (and_2_out, A, C);
  and and_3 (and_3_out, B, C);
  not not_1 (not_1_out, B);
  not not_2 (not_2_out, A);
  and and_4 (and_4_out, not_2_out, not_1_out, C);
  not not_3 (not_3_out, A);
  not not_4 (not_4_out, C);
  and and_5 (and_5_out, not_3_out, B, not_4_out);
  or or_2 (S, and_4_out, and_5_out, and_6_out, and_7_out);
  and and_6 (and_6_out, A, B, C);
  not not_5 (not_5_out, C);
  not not_6 (not_6_out, B);
  and and_7 (and_7_out, A, not_6_out, not_5_out);
endmodule
