// Logisim project adicao_binaria_vai_um_xor.circ as structural Verilog: 1 circuit, main circuit main
module main (
  input  A,
  input  B,
  input  C,
  output C_out,
  output S
);

  wire and_1_out, and_2_out, and_3_out, xor_1_out;

  or or_1 (C_out, and_1_out, and_2_out, and_3_out);
  and and_1 (and_1_out, A, B);
  and and_2 (and_2_out, A, C);
  and and_3 (and_3_out, B, C);
  xor xor_1 (xor_1_out, A, B);
  xor xor_2 (S, xor_1_out, C);
endmodule
