// Logisim project decode_3x8.circ as structural Verilog: 1 circuit, main circuit main
module main (
  input  in_1,
  input  in_2,
  input  in_3,
  output out_4,
  output out_5,
  output out_6,
  output out_7,
  output out_8,
  output out_9,
  output out_10,
  output out_11
);

  wire not_1_out, not_2_out, not_3_out;

  not not_1 (not_1_out, in_2);
  not not_2 (not_2_out, in_1);
  not not_3 (not_3_out, in_3);
  and _000 (out_4, not_3_out, not_1_out, not_2_out);
  and _001 (out_5, not_2_out, not_1_out, in_3);
  and _010 (out_6, not_2_out, in_2, not_3_out);
  and _011 (out_7, not_2_out, in_2, in_3);
  and _100 (out_8, in_1, not_1_out, not_3_out);
  and _101 (out_9, in_1, not_1_out, in_3);
  and _110 (out_10, in_1, in_2, not_3_out);
  and _111 (out_11, in_1, in_2, in_3);
endmodule
