// Logisim project decode_4x16.circ as structural Verilog: 1 circuit, main circuit main
module main (
  input  in_1,
  input  in_2,
  input  in_3,
  input  in_4,
  output out_5,
  output out_6,
  output out_7,
  output out_8,
  output out_9,
  output out_10,
  output out_11,
  output out_12,
  output out_13,
  output out_14,
  output out_15,
  output out_16,
  output out_17,
  output out_18,
  output out_19,
  output out_20
);

  wire not_1_out, not_2_out, not_3_out, not_4_out;

  not not_1 (not_1_out, in_1);
  not not_2 (not_2_out, in_2);
  not not_3 (not_3_out, in_3);
  not not_4 (not_4_out, in_4);
  and _000 (out_5, not_1_out, not_2_out, not_3_out, not_4_out);
  and _001 (out_6, not_1_out, not_2_out, not_3_out, in_4);
  and _010 (out_7, not_1_out, not_2_out, in_3, not_4_out);
  and _011 (out_8, not_1_out, not_2_out, in_3, in_4);
  and _100 (out_9, not_1_out, in_2, not_3_out, not_4_out);
  and _101 (out_10, not_1_out, in_2, not_3_out, in_4);
  and _110 (out_11, not_1_out, in_2, in_3, not_4_out);
  and _111 (out_12, not_1_out, in_2, in_3, in_4);
  and _000_2 (out_13, in_1, not_2_out, not_3_out, not_4_out);
  and _001_2 (out_14, in_1, not_2_out, not_3_out, in_4);
  and _010_2 (out_15, in_1, not_2_out, in_3, not_4_out);
  and _011_2 (out_16, in_1, not_2_out, in_3, in_4);
  and _100_2 (out_17, in_1, in_2, not_3_out, not_4_out);
  and _101_2 (out_18, in_1, in_2, not_3_out, in_4);
  and _110_2 (out_19, in_1, in_2, in_3, not_4_out);
  and _111_2 (out_20, in_1, in_2, in_3, in_4);
endmodule
