// Logisim project rom_64bits.circ as structural Verilog: 2 circuits, main circuit main
module main (
  input  in_1,
  input  in_2,
  input  in_3,
  input  in_4,
  output out_5,
  output out_6,
  output out_7,
  output out_8
);

  wire demux_4x16_1_out_5, demux_4x16_1_out_6, demux_4x16_1_out_7, demux_4x16_1_out_8, demux_4x16_1_out_9,
       demux_4x16_1_out_10, demux_4x16_1_out_11, demux_4x16_1_out_12, demux_4x16_1_out_13,
       demux_4x16_1_out_14, demux_4x16_1_out_15, demux_4x16_1_out_16, demux_4x16_1_out_17,
       demux_4x16_1_out_18, demux_4x16_1_out_19, demux_4x16_1_out_20;

  demux_4x16 demux_4x16_1 (
    .out_5(demux_4x16_1_out_5), .out_6(demux_4x16_1_out_6), .out_7(demux_4x16_1_out_7),
    .out_8(demux_4x16_1_out_8), .out_9(demux_4x16_1_out_9), .out_10(demux_4x16_1_out_10),
    .out_11(demux_4x16_1_out_11), .out_12(demux_4x16_1_out_12), .out_13(demux_4x16_1_out_13),
    .out_14(demux_4x16_1_out_14), .out_15(demux_4x16_1_out_15), .out_16(demux_4x16_1_out_16),
    .out_17(demux_4x16_1_out_17), .out_18(demux_4x16_1_out_18), .out_19(demux_4x16_1_out_19),
    .out_20(demux_4x16_1_out_20), .in_1(in_1), .in_2(in_2), .in_3(in_3), .in_4(in_4));
  or or_1 (out_5, demux_4x16_1_out_20, demux_4x16_1_out_19, demux_4x16_1_out_18, demux_4x16_1_out_17, demux_4x16_1_out_16, demux_4x16_1_out_15, demux_4x16_1_out_14, demux_4x16_1_out_13);
  or or_2 (out_6, demux_4x16_1_out_16, demux_4x16_1_out_15, demux_4x16_1_out_14, demux_4x16_1_out_13, demux_4x16_1_out_12, demux_4x16_1_out_11, demux_4x16_1_out_10, demux_4x16_1_out_9);
  or or_3 (out_7, demux_4x16_1_out_18, demux_4x16_1_out_17, demux_4x16_1_out_16, demux_4x16_1_out_15, demux_4x16_1_out_10, demux_4x16_1_out_9, demux_4x16_1_out_8, demux_4x16_1_out_7);
  or or_4 (out_8, demux_4x16_1_out_19, demux_4x16_1_out_18, demux_4x16_1_out_15, demux_4x16_1_out_14, demux_4x16_1_out_11, demux_4x16_1_out_10, demux_4x16_1_out_7, demux_4x16_1_out_6);
endmodule

module demux_4x16 (
  input  in_1,
  input  in_2,
  input  in_3,
  input  in_4,
  output out_5,
  output out_6,
  output out_7,
  output out_8,
  output out_9,
  output out_10,
  output out_11,
  output out_12,
  output out_13,
  output out_14,
  output out_15,
  output out_16,
  output out_17,
  output out_18,
  output out_19,
  output out_20
);

  wire not_1_out, not_2_out, not_3_out, not_4_out;

  not not_1 (not_1_out, in_2);
  not not_2 (not_2_out, in_1);
  not not_3 (not_3_out, in_3);
  not not_4 (not_4_out, in_4);
  and _000 (out_5, not_2_out, not_1_out, not_3_out, not_4_out);
  and _001 (out_6, not_2_out, not_1_out, not_3_out, in_4);
  and _010 (out_7, not_2_out, not_1_out, in_3, not_4_out);
  and _011 (out_8, not_2_out, not_1_out, in_3, in_4);
  and _100 (out_9, not_2_out, in_2, not_3_out, not_4_out);
  and _101 (out_10, not_2_out, in_2, not_3_out, in_4);
  and _110 (out_11, not_2_out, in_2, in_3, not_4_out);
  and _111 (out_12, not_2_out, in_2, in_3, in_4);
  and _000_2 (out_13, in_1, not_1_out, not_3_out, not_4_out);
  and _001_2 (out_14, in_1, not_1_out, not_3_out, in_4);
  and _010_2 (out_15, in_1, not_1_out, in_3, not_4_out);
  and _011_2 (out_16, in_1, not_1_out, in_3, in_4);
  and _100_2 (out_17, in_1, in_2, not_3_out, not_4_out);
  and _101_2 (out_18, in_1, in_2, not_3_out, in_4);
  and _110_2 (out_19, in_1, in_2, in_3, not_4_out);
  and _111_2 (out_20, in_1, in_2, in_3, in_4);
endmodule
