// Logisim project somador_4bis_carry_lookyahead.circ as structural Verilog: 2 circuits, main circuit main
module main (
  input  B3,
  input  B2,
  input  B1,
  input  B0,
  input  A3,
  input  A2,
  input  A1,
  input  A0,
  input  _0,
  output S3,
  output S2,
  output S1,
  output S0
);

  wire and_1_out, and_2_out, and_3_out, and_4_out, and_5_out, and_6_out, and_7_out, and_8_out, and_9_out,
       and_10_out, C0_out, C1_out, C2_out;

  or C2 (C2_out, and_1_out, and_2_out, and_3_out, and_4_out, and_5_out, and_6_out, and_7_out);
  adicao_binaria_xor adicao_binaria_xor_1 (.C(C2_out), .A(A3), .B(B3), .S(S3));
  and and_1 (and_1_out, A2, B2);
  and and_2 (and_2_out, A2, A1, B1);
  and and_3 (and_3_out, A2, A1, A0, B0);
  and and_4 (and_4_out, A2, B1, A0, B0);
  and and_5 (and_5_out, B2, A1, C0_out);
  and and_6 (and_6_out, A2, A1, A0, B0);
  and and_7 (and_7_out, A2, B1, A0, B0);
  or C1 (C1_out, and_8_out, and_9_out, and_10_out);
  adicao_binaria_xor adicao_binaria_xor_2 (.C(C1_out), .A(A2), .B(B2), .S(S2));
  and and_8 (and_8_out, A1, B1);
  and and_9 (and_9_out, A1, A0, B0);
  and and_10 (and_10_out, B1, A0, B0);
  and C0 (C0_out, A0, B0);
  adicao_binaria_xor adicao_binaria_xor_3 (.C(C0_out), .A(A1), .B(B1), .S(S1));
  adicao_binaria_xor adicao_binaria_xor_4 (.C(_0), .A(A0), .B(B0), .S(S0));

  // Notes on the sheet:
  //   Somador de 4 bits com vai-um antecipado
  //   (carry lookahead)
  //   C3 omitido por ser muito grande!
endmodule

module adicao_binaria_xor (
  input  A,
  input  B,
  input  C,
  output S
);

  wire xor_1_out;

  xor xor_1 (xor_1_out, A, B);
  xor xor_2 (S, xor_1_out, C);
endmodule
