// Logisim project somador_4bis_carry_lookyahead_completo.circ as structural Verilog: 2 circuits, main circuit main
module main (
  input  B3,
  input  B2,
  input  B1,
  input  B0,
  input  A3,
  input  A2,
  input  A1,
  input  A0,
  input  C_in,
  output C_out,
  output S3,
  output S2,
  output S1,
  output S0
);

  wire and_1_out, and_2_out, and_3_out, and_4_out, and_5_out, and_6_out, and_7_out, and_8_out, and_9_out,
       and_10_out, and_11_out, and_12_out, and_13_out, and_14_out, and_15_out, and_16_out, and_17_out,
       and_18_out, and_19_out, and_20_out, and_21_out, and_22_out, and_23_out, and_24_out, and_25_out,
       and_26_out, or_2_out, or_3_out;

  or or_1 (C_out, and_1_out, and_2_out, and_3_out, and_4_out, and_5_out, and_6_out, and_7_out, and_8_out, and_9_out, and_10_out, and_11_out, and_12_out, and_13_out, and_14_out, and_15_out);
  and and_1 (and_1_out, A3, B3);
  and and_2 (and_2_out, A3, and_16_out);
  and and_3 (and_3_out, A3, and_17_out);
  and and_4 (and_4_out, A3, and_18_out);
  and and_5 (and_5_out, A3, and_19_out);
  and and_6 (and_6_out, A3, and_20_out);
  and and_7 (and_7_out, A3, and_21_out);
  and and_8 (and_8_out, A3, and_22_out);
  and and_9 (and_9_out, B3, and_16_out);
  and and_10 (and_10_out, B3, and_17_out);
  and and_11 (and_11_out, B3, and_18_out);
  and and_12 (and_12_out, B3, and_19_out);
  and and_13 (and_13_out, B3, and_20_out);
  and and_14 (and_14_out, B3, and_21_out);
  and and_15 (and_15_out, B3, and_22_out);
  adicao_binaria_xor adicao_binaria_xor_1 (.S(S3), .A(A3), .B(B3), .C_in(or_2_out));
  or or_2 (or_2_out, and_16_out, and_17_out, and_18_out, and_19_out, and_20_out, and_21_out, and_22_out);
  and and_16 (and_16_out, A2, B2);
  and and_17 (and_17_out, A2, and_23_out);
  and and_18 (and_18_out, A2, and_24_out);
  and and_19 (and_19_out, A2, and_25_out);
  and and_20 (and_20_out, B2, and_23_out);
  and and_21 (and_21_out, B2, and_24_out);
  and and_22 (and_22_out, B2, and_25_out);
  adicao_binaria_xor adicao_binaria_xor_2 (.S(S2), .A(A2), .B(B2), .C_in(or_3_out));
  or or_3 (or_3_out, and_23_out, and_24_out, and_25_out);
  and and_23 (and_23_out, A1, B1);
  and and_24 (and_24_out, A1, and_26_out);
  and and_25 (and_25_out, B1, and_26_out);
  adicao_binaria_xor adicao_binaria_xor_3 (.S(S1), .A(A1), .B(B1), .C_in(and_26_out));
  and and_26 (and_26_out, A0, B0);
  adicao_binaria_xor adicao_binaria_xor_4 (.S(S0), .A(A0), .B(B0), .C_in(C_in));
endmodule

module adicao_binaria_xor (
  input  A,
  input  B,
  input  C_in,
  output S
);

  wire xor_1_out;

  xor xor_1 (xor_1_out, A, B);
  xor xor_2 (S, xor_1_out, C_in);
endmodule
