// Logisim project somador_4bits_simples.circ as structural Verilog: 2 circuits, main circuit main
module main (
  input  in_1,
  input  in_2,
  input  in_3,
  input  in_4,
  input  in_5,
  input  in_6,
  input  in_7,
  input  in_8,
  input  in_9,
  output out_10,
  output out_11,
  output out_12,
  output out_13,
  output out_14
);

  wire adicao_binaria_vai_um_2_c_out, adicao_binaria_vai_um_3_c_out, adicao_binaria_vai_um_4_c_out;

  adicao_binaria_vai_um adicao_binaria_vai_um_1 (
    .A(in_5), .B(in_1), .C(adicao_binaria_vai_um_2_c_out), .C_out(out_10), .S(out_11));
  adicao_binaria_vai_um adicao_binaria_vai_um_2 (
    .A(in_6), .B(in_2), .C(adicao_binaria_vai_um_3_c_out), .C_out(adicao_binaria_vai_um_2_c_out), .S(out_12));
  adicao_binaria_vai_um adicao_binaria_vai_um_3 (
    .A(in_7), .B(in_3), .C(adicao_binaria_vai_um_4_c_out), .C_out(adicao_binaria_vai_um_3_c_out), .S(out_13));
  adicao_binaria_vai_um adicao_binaria_vai_um_4 (
    .A(in_8), .B(in_4), .C(in_9), .C_out(adicao_binaria_vai_um_4_c_out), .S(out_14));
endmodule

module adicao_binaria_vai_um (
  input  A,
  input  B,
  input  C,
  output C_out,
  output S
);

  wire and_1_out, and_2_out, and_3_out, and_4_out, and_5_out, and_6_out, and_7_out, not_1_out, not_2_out,
       not_3_out, not_4_out, not_5_out, not_6_out;

  and and_1 (and_1_out, A, B);
  or or_1 (C_out, and_1_out, and_2_out, and_3_out);
  and and_2 (and_2_out, A, C);
  and and_3 (and_3_out, B, C);
  not not_1 (not_1_out, A);
  not not_2 (not_2_out, A);
  not not_3 (not_3_out, B);
  and and_4 (and_4_out, not_1_out, not_3_out, C);
  and and_5 (and_5_out, not_2_out, B, not_4_out);
  not not_4 (not_4_out, C);
  and and_6 (and_6_out, A, B, C);
  or or_2 (S, and_4_out, and_5_out, and_6_out, and_7_out);
  not not_5 (not_5_out, C);
  not not_6 (not_6_out, B);
  and and_7 (and_7_out, A, not_6_out, not_5_out);
endmodule
