// Logisim project contador_assincrono_4_bits_LS.circ as structural Verilog: 1 circuit, main circuit main
module main (
  output [3:0] out_1,
  output out_2,
  output out_3,
  output out_4,
  output out_5,
  output [3:0] out_6,
  output out_7,
  output out_8,
  output out_9,
  output out_10
);

  wire clock_1_out, clock_2_out, j_k_ff_2_q, j_k_ff_4_q, j_k_ff_6_q, j_k_ff_8_q;

  Clock clock_1 (.out(clock_1_out));
  Clock clock_2 (.out(clock_2_out));
  J_K_Flip_Flop j_k_ff_1 (.J(1'b1), .clk(clock_1_out), .K(1'b1), .Q(out_1[0]));  // open: Qn, preset, en, reset
  J_K_Flip_Flop j_k_ff_2 (.J(1'b1), .clk(clock_2_out), .K(1'b1), .Q(j_k_ff_2_q));  // open: Qn, preset, en, reset
  not not_1 (out_6[0], j_k_ff_2_q);
  J_K_Flip_Flop j_k_ff_3 (.J(1'b1), .clk(out_1[0]), .K(1'b1), .Q(out_1[1]));  // open: Qn, preset, en, reset
  J_K_Flip_Flop j_k_ff_4 (.J(1'b1), .clk(j_k_ff_2_q), .K(1'b1), .Q(j_k_ff_4_q));  // open: Qn, preset, en, reset
  not not_2 (out_6[1], j_k_ff_4_q);
  J_K_Flip_Flop j_k_ff_5 (.J(1'b1), .clk(out_1[1]), .K(1'b1), .Q(out_1[2]));  // open: Qn, preset, en, reset
  J_K_Flip_Flop j_k_ff_6 (.J(1'b1), .clk(j_k_ff_4_q), .K(1'b1), .Q(j_k_ff_6_q));  // open: Qn, preset, en, reset
  not not_3 (out_6[2], j_k_ff_6_q);
  J_K_Flip_Flop j_k_ff_7 (.J(1'b1), .clk(out_1[2]), .K(1'b1), .Q(out_1[3]));  // open: Qn, preset, en, reset
  J_K_Flip_Flop j_k_ff_8 (.J(1'b1), .clk(j_k_ff_6_q), .K(1'b1), .Q(j_k_ff_8_q));  // open: Qn, preset, en, reset
  not not_4 (out_6[3], j_k_ff_8_q);

  assign out_2 = out_1[0];
  assign out_3 = out_1[1];
  assign out_4 = out_1[2];
  assign out_5 = out_1[3];
  assign out_7 = out_6[0];
  assign out_8 = out_6[1];
  assign out_9 = out_6[2];
  assign out_10 = out_6[3];

  // Notes on the sheet:
  //   Contador assíncrono - 4  bits
  //   Obs.: Para corrigir a saída, foi necessário incluir portas NOT
endmodule
