// Logisim project contador_sincrono_LS.circ as structural Verilog: 1 circuit, main circuit main
module main (
  output [2:0] out_1,
  output A,
  output B,
  output C
);

  wire and_1_out, Clock_out;

  Clock Clock (.out(Clock_out));
  J_K_Flip_Flop j_k_ff_1 (.J(1'b1), .clk(Clock_out), .K(1'b1), .Q(A));  // open: Qn, preset, en, reset
  J_K_Flip_Flop j_k_ff_2 (.J(A), .clk(Clock_out), .K(A), .Q(B));  // open: Qn, preset, en, reset
  and and_1 (and_1_out, A, B);
  J_K_Flip_Flop j_k_ff_3 (.J(and_1_out), .clk(Clock_out), .K(and_1_out), .Q(C));  // open: Qn, preset, en, reset

  assign out_1 = {C, B, A};

  // Notes on the sheet:
  //   Contador síncrono - 3 bits
endmodule
