// Logisim project flip_flop_sr_clock.circ as structural Verilog: 1 circuit, main circuit main
module main (
  input  R,
  input  Clock,
  input  S,
  output Q,
  output Q_prime
);

  wire and_1_out, and_2_out;

  and and_1 (and_1_out, R, Clock);
  and and_2 (and_2_out, Clock, S);
  nor nor_1 (Q, and_1_out, Q_prime);
  nor nor_2 (Q_prime, Q, and_2_out);

  // Notes on the sheet:
  //   Flip-flop S-R com relógio
endmodule
