// Logisim project flip_flop_tipo_jk_LS.circ as structural Verilog: 1 circuit, main circuit main
module main (
  input  J,
  input  Clock,
  input  K,
  output Q,
  output Q_prime
);

  J_K_Flip_Flop j_k_ff_1 (.J(J), .clk(Clock), .K(K), .Q(Q), .Qn(Q_prime));  // open: preset, en, reset

  // Notes on the sheet:
  //   Flip-flop J-K
endmodule
