// Logisim project registrador_desloc_5_bits_dir_esq_LS.circ as structural Verilog: 1 circuit, main circuit main
module main (
  input  in_1,
  input  in_2,
  output [5:0] out_3,
  output S0,
  output S1,
  output S2,
  output S3,
  output out_8,
  output out_9,
  output [5:0] out_10,
  output S5,
  output S4,
  output S3_2,
  output S2_2,
  output S1_2,
  output S0_2
);

  wire clock_1_out, clock_2_out, not_1_out, not_2_out, s_r_ff_1_qn, s_r_ff_2_qn, s_r_ff_3_qn, s_r_ff_4_qn,
       s_r_ff_5_qn, s_r_ff_6_qn, s_r_ff_7_qn, s_r_ff_8_qn, s_r_ff_9_qn, s_r_ff_10_qn;

  Clock clock_1 (.out(clock_1_out));
  Clock clock_2 (.out(clock_2_out));
  not not_1 (not_1_out, in_1);
  not not_2 (not_2_out, in_2);
  S_R_Flip_Flop s_r_ff_1 (
    .S(in_1), .clk(clock_1_out), .R(not_1_out), .Q(out_3[0]), .Qn(s_r_ff_1_qn));  // open: preset, reset, en
  S_R_Flip_Flop s_r_ff_2 (
    .S(in_2), .clk(clock_2_out), .R(not_2_out), .Q(out_10[5]), .Qn(s_r_ff_2_qn));  // open: preset, reset, en
  S_R_Flip_Flop s_r_ff_3 (
    .S(out_3[0]), .clk(clock_1_out), .R(s_r_ff_1_qn), .Q(out_3[1]), .Qn(s_r_ff_3_qn));  // open: preset, reset, en
  S_R_Flip_Flop s_r_ff_4 (
    .S(out_10[5]), .clk(clock_2_out), .R(s_r_ff_2_qn), .Q(out_10[4]), .Qn(s_r_ff_4_qn));  // open: preset, reset, en
  S_R_Flip_Flop s_r_ff_5 (
    .S(out_3[1]), .clk(clock_1_out), .R(s_r_ff_3_qn), .Q(out_3[2]), .Qn(s_r_ff_5_qn));  // open: preset, reset, en
  S_R_Flip_Flop s_r_ff_6 (
    .S(out_10[4]), .clk(clock_2_out), .R(s_r_ff_4_qn), .Q(out_10[3]), .Qn(s_r_ff_6_qn));  // open: preset, reset, en
  S_R_Flip_Flop s_r_ff_7 (
    .S(out_3[2]), .clk(clock_1_out), .R(s_r_ff_5_qn), .Q(out_3[3]), .Qn(s_r_ff_7_qn));  // open: preset, reset, en
  S_R_Flip_Flop s_r_ff_8 (
    .S(out_10[3]), .clk(clock_2_out), .R(s_r_ff_6_qn), .Q(out_10[2]), .Qn(s_r_ff_8_qn));  // open: preset, reset, en
  S_R_Flip_Flop s_r_ff_9 (
    .S(out_3[3]), .clk(clock_1_out), .R(s_r_ff_7_qn), .Q(out_3[4]), .Qn(s_r_ff_9_qn));  // open: preset, reset, en
  S_R_Flip_Flop s_r_ff_10 (
    .S(out_10[2]), .clk(clock_2_out), .R(s_r_ff_8_qn), .Q(out_10[1]), .Qn(s_r_ff_10_qn));  // open: preset, reset, en
  S_R_Flip_Flop s_r_ff_11 (
    .S(out_3[4]), .clk(clock_1_out), .R(s_r_ff_9_qn), .Q(out_3[5]));  // open: Qn, preset, reset, en
  S_R_Flip_Flop s_r_ff_12 (
    .S(out_10[1]), .clk(clock_2_out), .R(s_r_ff_10_qn), .Q(out_10[0]));  // open: Qn, preset, reset, en

  assign out_8 = out_3[4];
  assign out_9 = out_3[5];
  assign S0 = out_3[0];
  assign S0_2 = out_10[0];
  assign S1 = out_3[1];
  assign S1_2 = out_10[1];
  assign S2 = out_3[2];
  assign S2_2 = out_10[2];
  assign S3 = out_3[3];
  assign S3_2 = out_10[3];
  assign S4 = out_10[4];
  assign S5 = out_10[5];

  // Notes on the sheet:
  //   Bit menos significativo
  //   Bit mais significativo
  //   Registrador de deslocamento - a esquerda
  //   Registrador de deslocamento -  a direita
  //   Bit mais significativo
  //   Bit menos significativo
endmodule
