// Logisim project registrador_paralelo_8_bits.circ as structural Verilog: 2 circuits, main circuit main
module main (
  input  I7,
  input  I6,
  input  I5,
  input  I4,
  input  I3,
  input  I2,
  input  I1,
  input  I0,
  input  in_9,
  input  LInha_de_reset,
  input  in_11,
  output O7,
  output out_13,
  output out_14,
  output out_15,
  output out_16,
  output out_17,
  output out_18,
  output O0
);

  wire and_1_out, and_3_out, and_5_out, and_6_out, and_9_out, and_10_out, and_12_out, and_15_out,
       flip_flop_sr_1_q, flip_flop_sr_2_q, flip_flop_sr_3_q, flip_flop_sr_4_q, flip_flop_sr_5_q,
       flip_flop_sr_6_q, flip_flop_sr_7_q, flip_flop_sr_8_q;

  and and_1 (and_1_out, in_9, I7);
  flip_flop_sr flip_flop_sr_1 (.R(LInha_de_reset), .S(and_1_out), .Q(flip_flop_sr_1_q));  // open: Q_prime
  and and_2 (O7, in_11, flip_flop_sr_1_q);
  and and_3 (and_3_out, in_9, I6);
  and and_4 (out_13, in_11, flip_flop_sr_2_q);
  and and_5 (and_5_out, in_9, I5);
  flip_flop_sr flip_flop_sr_2 (.R(LInha_de_reset), .S(and_3_out), .Q(flip_flop_sr_2_q));  // open: Q_prime
  and and_6 (and_6_out, in_9, I4);
  flip_flop_sr flip_flop_sr_3 (.R(LInha_de_reset), .S(and_5_out), .Q(flip_flop_sr_3_q));  // open: Q_prime
  and and_7 (out_14, in_11, flip_flop_sr_3_q);
  flip_flop_sr flip_flop_sr_4 (.R(LInha_de_reset), .S(and_6_out), .Q(flip_flop_sr_4_q));  // open: Q_prime
  and and_8 (out_15, in_11, flip_flop_sr_4_q);
  and and_9 (and_9_out, in_9, I3);
  and and_10 (and_10_out, in_9, I2);
  flip_flop_sr flip_flop_sr_5 (.R(LInha_de_reset), .S(and_9_out), .Q(flip_flop_sr_5_q));  // open: Q_prime
  and and_11 (out_16, in_11, flip_flop_sr_5_q);
  and and_12 (and_12_out, in_9, I1);
  flip_flop_sr flip_flop_sr_6 (.R(LInha_de_reset), .S(and_10_out), .Q(flip_flop_sr_6_q));  // open: Q_prime
  and and_13 (out_17, in_11, flip_flop_sr_6_q);
  flip_flop_sr flip_flop_sr_7 (.R(LInha_de_reset), .S(and_12_out), .Q(flip_flop_sr_7_q));  // open: Q_prime
  and and_14 (out_18, in_11, flip_flop_sr_7_q);
  and and_15 (and_15_out, in_9, I0);
  flip_flop_sr flip_flop_sr_8 (.R(LInha_de_reset), .S(and_15_out), .Q(flip_flop_sr_8_q));  // open: Q_prime
  and and_16 (O0, in_11, flip_flop_sr_8_q);

  // Notes on the sheet:
  //   Habiltação de entrada
  //   Habiltação de saída
  //   Registrador paralelo de 8 bits
  //   Linhas de dados de entrada
endmodule

module flip_flop_sr (
  input  R,
  input  S,
  output Q,
  output Q_prime
);

  nor nor_1 (Q, R, Q_prime);
  nor nor_2 (Q_prime, Q, S);
endmodule
